# Fritzing sketch external-led-pot (saved by Fritzing 0.9.3b)
breadboards: 1

parts:
  Part1 = Arduino Uno (Rev3)
  LED1 = smd LED [color="Red (633nm)" package="0603 [SMD]"]
  R1 = Resistor [tolerance=±5% resistance=10k package="2512 [SMD]"]
  R2 = TRIMPOT [package=3362u-2]
  R3 = Resistor [tolerance=±5% resistance=10k package="2512 [SMD]"]

nets (from the breadboard view):
  N1: Part1.A0, R2.WIPER
  N2: Part1.D13/SCK, R1.Pin_1
  N3: Part1.GND, LED1.cathode, R2.CCW
  N4: LED1.anode, R1.Pin_0
  N5: R2.CW, R3.Pin_0
